# Fritzing sketch PN532 SPI (saved by Fritzing 0.9.3b)

parts:
  Part1 = Adafruit PN532 Breakout [part_number="Adafruit #364"]
  Part4 = Adafruit 4-channel I2C-safe Bi-directional Logic Level Converter [part_number="Adafruit #757"]
  Part2 = Arduino Uno (Rev3) - ICSP

nets (from the schematic view):
  N1: Part1.VDD, Part1.SEL1, Part4.LV
  GND: Part1.SEL0, Part1.GND, Part4.GND, Part2.GND
  N2: Part1.MOSI/SDA/TX, Part4.A2
  N3: Part1.NSS/SCL/RX, Part4.A3
  N4: Part1.IRQ, Part4.A4
  N5: Part1.+5.0V, Part4.HV, Part2.5V
  N6: Part4.B4, Part2.D2
  N7: Part4.B3, Part2.A5/SCL
  N8: Part4.B2, Part2.A4/SDA
  N9: Part2.ICSP_MISO, Part2.D12/MISO
  N10: Part2.ICSP_MOSI, Part2.D11_PWM/MOSI

notes:
  To enable SPI mode, ensure jumpers are set as indicated:
  [SEL0] OFF, [SEL1] ON
  PN532 operates at 3.3V, but Arduino UNO is 5V, so need bi-directional level shifter on MOSI, SCK, and SSEL lines (not strictly required on MISO - a 3.3V HIGH will still be read as HIGH by 5V Arduino, but does no harm)
  LV <-> PN532 3.3V (or Arduino 3.3V)
  L1 <-> PN532 SCK
  L2 <-> PN532 MISO
  L3 <-> PN532 MOSI/SDA/TX
  L4 <-> PN532 SSEL/SCL/RX
  GND <-> PN532 GND
  HV <-> Arduino 5V or ICSP-2
  H1 <-> Arduino 13 or ICSP-3
  H2 <-> Arduino 12 or ICSP-1
  H3 <-> Arduino 11 or ICSP-4
  H4 <-> Arduino 10
  GND <-> Arduino GND or ICSP-6
  Arduino SPI pins are mapped to digital GPIO pins as well as the separate ICSP header - use whichever is most convenient.
  SCK - Pin 13 or ICSP-3
  MISO Pin 12 or ICSP-1
  MOSI Pin 11 or ICSP-4
  SS pin is shown here using digital pin 10, but this can be adjusted in code.
  PN532 Breakout Board
  Even though PN532 chip itself operates @3.3V, the board requires 5V input from Arduino. The 3.3V pin on the breakout can instead be used as an output to the low voltage pin on the level shifter.
  3.3V <-> Level Shifter LV
  SCK <-> Level Shifter LV1
  MISO <-> Level Shifter L2
  MOSI/SDA/TX <-> Level Shifter L3
  SSEL/SCL/RX <-> Level Shifter L4
  GND <-> Level Shifter GND
  5.0V <-> Arduino 5V

custom parts:
  Adafruit PN532 Breakout: The PN532 is the most popular NFC chip, and is what is embedded in pretty much every phone or device that does NFC. It can pretty much do it all, such as read and write to tags and cards, communicate with phones (say for payment processing), and 'act' like a NFC tag. If you want to do any sort of embedded NFC work, this is the chip you'll want to use! NFC (Near Field Communications) is a way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
  Adafruit 4-channel I2C-safe Bi-directional Logic Level Converter: Because the Arduino (and Basic Stamp) are 5V devices, and most modern sensors, displays, flash cards and modes are 3.3V-only, many makers find that they need to perform level shifting/conversion to protect the 3.3V device from 5V. We do have some other handy level shifters in the shop, from the DIP 74LVC245 to the fancy bi-directional TXB0108. However, neither of these are happy to work with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
